# Fritzing sketch nrf24l01 conection (saved by Fritzing 0.9.2b)
breadboards: 1

parts:
  NRF24L1 = NRF24L01
  元件1 = Arduino Micro (Rev3)  # not connected
  元件2 = Arduino Nano (Rev3.0) (ICSP)
  NRF24L2 = NRF24L01  # not connected
  元件3 = Arduino Micro (Rev3)  # not connected

nets:
  VCC: NRF24L1.VCC, 元件2.3V3
  N1: NRF24L1.CSN, 元件2.D10
  N2: NRF24L1.MOSI, 元件2.D11/MOSI
  N3: NRF24L1.IRQ, NRF24L1.MISO, 元件2.D12/MISO
  GND: NRF24L1.GND, 元件2.GND
  N4: NRF24L1.CE, 元件2.D9
  N5: NRF24L1.SCK, 元件2.D13/SCK

custom parts:
  NRF24L01: NRF24L01 module
